// Logisim project index.circ as structural Verilog
module main (
  input  [7:0] in_1,
  input  [7:0] in_2,
  input  in_3,
  input  in_4,
  input  Binvert
);

  wire and_1_out, C_2_out, C_out, Clock__15_Cliques_out, mux_1_output, or_1_out, somador_1_output, undriven,
       xor_1_out, xor_2_out;
  wire [3:0] registrador_1_q0, registrador_1_q4, registrador_2_q0, registrador_2_q4;

  Clock Clock__15_Cliques (.out(Clock__15_Cliques_out));
  Hex_Digit_Display hex_digit_display_1 (.value(registrador_1_q0));  // open: dp
  Hex_Digit_Display hex_digit_display_2 (.value(registrador_1_q4));  // open: dp
  Button C (.out(C_out));
  registrador registrador_1 (
    .Clock(Clock__15_Cliques_out), .Q7(registrador_1_q4[3]), .Q6(registrador_1_q4[2]),
    .Q5(registrador_1_q4[1]), .Q4(registrador_1_q4[0]), .Q3(registrador_1_q0[3]), .Q2(registrador_1_q0[2]),
    .Q1(registrador_1_q0[1]), .Q0(registrador_1_q0[0]), .Clear(C_out), .Input__8_Bits(in_1));  // open: C_In
  Hex_Digit_Display hex_digit_display_3 (.value(registrador_2_q4));  // open: dp
  Hex_Digit_Display hex_digit_display_4 (.value(registrador_2_q0));  // open: dp
  Button C_2 (.out(C_2_out));
  registrador registrador_2 (
    .C_In(1'b0), .Clock(Clock__15_Cliques_out), .Q7(registrador_2_q4[3]), .Q6(registrador_2_q4[2]),
    .Q5(registrador_2_q4[1]), .Q4(registrador_2_q4[0]), .Q3(registrador_2_q0[3]), .Q2(registrador_2_q0[2]),
    .Q1(registrador_2_q0[1]), .Q0(registrador_2_q0[0]), .Clear(C_2_out), .Input__8_Bits(in_2));
  and and_1 (and_1_out, registrador_1_q0[0], undriven);
  or or_1 (or_1_out, registrador_1_q0[0], undriven);
  xor xor_1 (xor_1_out, registrador_1_q0[0], undriven);
  somador somador_1 (.A(registrador_1_q0[0]), .B(xor_2_out), .Clock(Clock__15_Cliques_out), .Output(somador_1_output));
  xor xor_2 (xor_2_out, undriven, Binvert);
  mux mux_1 (
    .S0(in_3), .S1(in_4), .D0(and_1_out), .D1(or_1_out), .D2(xor_1_out), .D3(somador_1_output),
    .Output(mux_1_output));
endmodule

module registrador (
  input  Clock,
  input  C_In,
  input  Clear,
  input  [7:0] Input__8_Bits,
  output Q7,
  output Q6,
  output Q5,
  output Q4,
  output Q3,
  output Q2,
  output Q1,
  output Q0
);

  D_Flip_Flop d_ff_1 (.clk(Clock), .D(C_In), .Q(Q7), .preset(Input__8_Bits[7]), .reset(Clear));  // open: Qn, en
  D_Flip_Flop d_ff_2 (.clk(Clock), .D(Q7), .Q(Q6), .preset(Input__8_Bits[6]), .reset(Clear));  // open: Qn, en
  D_Flip_Flop d_ff_3 (.clk(Clock), .D(Q6), .Q(Q5), .preset(Input__8_Bits[5]), .reset(Clear));  // open: Qn, en
  D_Flip_Flop d_ff_4 (.clk(Clock), .D(Q5), .Q(Q4), .preset(Input__8_Bits[4]), .reset(Clear));  // open: Qn, en
  D_Flip_Flop d_ff_5 (.clk(Clock), .D(Q4), .Q(Q3), .preset(Input__8_Bits[3]), .reset(Clear));  // open: Qn, en
  D_Flip_Flop d_ff_6 (.clk(Clock), .D(Q3), .Q(Q2), .preset(Input__8_Bits[2]), .reset(Clear));  // open: Qn, en
  D_Flip_Flop d_ff_7 (.clk(Clock), .D(Q2), .Q(Q1), .preset(Input__8_Bits[1]), .reset(Clear));  // open: Qn, en
  D_Flip_Flop d_ff_8 (.clk(Clock), .D(Q1), .Q(Q0), .preset(Input__8_Bits[0]), .reset(Clear));  // open: Qn, en
endmodule

// MUX
module mux (
  input  S0,
  input  S1,
  input  D0,
  input  D1,
  input  D2,
  input  D3,
  output Output
);

  wire and_1_out, and_2_out, and_3_out, and_4_out, not_1_out, not_2_out;

  not not_1 (not_1_out, S1);
  not not_2 (not_2_out, S0);
  and and_1 (and_1_out, not_1_out, D0, not_2_out);
  and and_2 (and_2_out, not_1_out, D1, S0);
  and and_3 (and_3_out, S1, D2, not_2_out);
  and and_4 (and_4_out, S1, D3, S0);
  or or_1 (Output, and_1_out, and_2_out, and_3_out, and_4_out);
endmodule

// FA
module somador (
  input  A,
  input  B,
  input  Clock,
  output Output
);

  wire and_1_out, and_2_out, d_ff_1_q, or_1_out, xor_1_out;

  D_Flip_Flop d_ff_1 (.clk(Clock), .D(or_1_out), .Q(d_ff_1_q));  // open: Qn, preset, en, reset
  xor xor_1 (xor_1_out, A, B);
  and and_1 (and_1_out, A, B);
  and and_2 (and_2_out, d_ff_1_q, xor_1_out);
  xor xor_2 (Output, xor_1_out, d_ff_1_q);
  or or_1 (or_1_out, and_2_out, and_1_out);
endmodule
